// Logisim project ALU.circ as structural Verilog: 1 circuit, main circuit ALU
module ALU (
  input  [31:0] A,
  input  [31:0] B,
  input  [4:0] Shift,
  input  [3:0] Codop,
  input  CarryIn,
  output [31:0] S,
  output [3:0] Flags
);

  wire [31:0] subtractor_1_out, Tadc, Tand, Tasr, Tbic, Tcmn, Tcmp, Tlsl, Tlsr, Tmul, Tmvn, Torr, Tror, Trsb,
       Tsbc, Ttst, Txor;

  assign Tand = A & B;  // AND_Gate and_1, 32 bits wide
  assign Txor = A ^ B;  // XOR_Gate xor_1, 32 bits wide
  Shifter #(.width(32)) shifter_1 (.in(B), .\dist (Shift), .out(Tlsl));
  Shifter #(.shift("lr"), .width(32)) shifter_2 (.in(B), .\dist (Shift), .out(Tlsr));
  Shifter #(.shift("ar"), .width(32)) shifter_3 (.in(B), .\dist (Shift), .out(Tasr));
  Adder #(.width(32)) adder_1 (.a(A), .b(B), .out(Tadc), .cin(CarryIn), .cout(Flags[2]));
  Subtractor #(.width(32)) subtractor_1 (.a(A), .b(B), .out(subtractor_1_out), .bin(CarryIn), .bout(Flags[2]));
  Subtractor #(.width(32)) subtractor_2 (.a(subtractor_1_out), .b(32'h1), .out(Tsbc));  // open: bin, bout
  assign Tmvn = ~B;  // NOT_Gate not_1, 32 bits wide
  Shifter #(.shift("rr"), .width(32)) shifter_4 (.in(B), .\dist (Shift), .out(Tror));
  assign Ttst = A & B;  // AND_Gate and_2, 32 bits wide
  Negator #(.width(32)) negator_1 (.in(A), .out(Trsb));
  Subtractor #(.width(32)) subtractor_3 (.a(A), .b(B), .out(Tcmp), .bout(Flags[2]));  // open: bin
  Adder #(.width(32)) adder_2 (.a(A), .b(B), .out(Tcmn), .cout(Flags[2]));  // open: cin
  assign Torr = A | B;  // OR_Gate or_1, 32 bits wide
  Multiplier #(.width(32)) multiplier_1 (.a(A), .b(B), .out(Tmul));  // open: cin, cout
  assign Tbic = ~(A & B);  // NAND_Gate nand_1, 32 bits wide
  Multiplexer #(.enable("false"), .select(4), .width(32)) multiplexer_1 (
    .in0(Tand), .in1(Txor), .in2(Tlsl), .in3(Tlsr), .in4(Tasr), .in5(Tadc), .in6(Tsbc), .in7(Tror),
    .in8(Ttst), .in9(Trsb), .in10(Tcmp), .in11(Tcmn), .in12(Torr), .in13(Tmul), .in14(Tbic), .in15(Tmvn),
    .out(S), .sel(Codop));
  Comparator #(.width(32)) comparator_1 (.a(S), .b({32{1'b0}}), .eq(Flags[1]), .lt(Flags[0]));  // open: gt

  // Other names for the same wires on the sheet: N = Flags[0]; Z = Flags[1]; C = Flags[2]; V = Flags[3];
  //   Sh[4:0] = Shift

  // Notes on the sheet:
  //   Note: for ROR, C = N
  //   Note 2: assume that shift > 0 for LSL and LSR
endmodule
