// Logisim project Ctl_Conditional.circ as structural Verilog: 1 circuit, main circuit Conditional
module Conditional (
  input  [15:0] Instruction,
  input  Z,
  input  C,
  input  N,
  input  V,
  input  Enable,
  output [10:0] Offset,
  output Verified
);

  wire comparator_1_eq, multiplexer_1_out, not_1_out, not_2_out, not_3_out, not_4_out, not_5_out, not_6_out,
       not_7_out, or_1_out, or_2_out, or_3_out, xor_1_out;
  wire [10:0] bit_extender_1_out;

  xor xor_1 (xor_1_out, N, V);
  or or_1 (or_1_out, ~C, Z);  // OR_Gate
  or or_2 (or_2_out, Z, xor_1_out);
  not not_1 (not_1_out, Z);
  not not_2 (not_2_out, C);
  not not_3 (not_3_out, N);
  not not_4 (not_4_out, V);
  not not_5 (not_5_out, or_1_out);
  Multiplexer #(.select(4)) multiplexer_1 (
    .in0(Z), .in1(not_1_out), .in2(C), .in3(not_2_out), .in4(N), .in5(not_3_out), .in6(V), .in7(not_4_out),
    .in8(not_5_out), .in9(or_1_out), .in10(not_6_out), .in11(xor_1_out), .in12(not_7_out), .in13(or_2_out),
    .in14(1'b1), .in15(1'b0), .out(multiplexer_1_out), .sel(Instruction[11:8]));
  not not_6 (not_6_out, xor_1_out);
  not not_7 (not_7_out, or_2_out);
  assign bit_extender_1_out = {{3{Instruction[7]}}, Instruction[7:0]};  // Bit_Extender bit_extender_1
  Comparator #(.width(4)) comparator_1 (.a(Instruction[15:12]), .b(4'b1110), .eq(comparator_1_eq));  // open: gt, lt
  Multiplexer #(.width(11)) multiplexer_2 (
    .in0(Instruction[10:0]), .in1(bit_extender_1_out), .out(Offset), .sel(Instruction[12]));
  or or_3 (or_3_out, comparator_1_eq, multiplexer_1_out);
  assign Verified = Enable ? or_3_out : 1'bz;  // Controlled_Buffer controlled_buffer_1
  Pull_Resistor pull_resistor_1 (.node(Verified));

  // Other names for the same wires on the sheet: Cond[3:0] = Instruction[11:8]; imm8[7:0] = Instruction[7:0]

  // Notes on the sheet:
  //   égalité
  //   différence
  //   retenue
  //   pas de retenue
  //   négatif
  //   positif ou nul
  //   dépassement de capacité
  //   pas de dépassement de capacité
  //   supérieur non signé
  //   inf ou égal non signé
  //   inf ou égal signé
  //   inf signé
  //   sup signé
  //   inf ou égal signé
  //   AL est toujours vrai
endmodule
