// Logisim project Ctl_Shift_Add_Sub_Mov.circ as structural Verilog: 1 circuit, main circuit Shift_Add_Sub_Mov
module Shift_Add_Sub_Mov (
  input  Enable,
  input  [15:0] Instruction,
  output [3:0] Flags_Update_Mask,
  output Carry,
  output Imm32_Enable,
  output [2:0] Rm,
  output [2:0] Rn,
  output [2:0] Rd,
  output [4:0] Imm5,
  output [31:0] Imm32,
  output [3:0] ALU_Opcode
);

  wire comparator_1_eq;
  wire [1:0] controlled_buffer_1_out;
  wire [3:0] multiplexer_1_out;

  Multiplexer #(.enable("false"), .select(2), .width(4)) multiplexer_1 (
    .in0(4'b0101), .in1(4'b0110), .in2(4'b1011), .in3(4'b1010), .out(multiplexer_1_out),
    .sel(Instruction[10:9]));
  assign controlled_buffer_1_out = comparator_1_eq ? Instruction[12:11] : 2'bz;  // Controlled_Buffer controlled_buffer_1
  Comparator #(.width(3)) comparator_1 (.a(Instruction[15:13]), .b(3'b000), .eq(comparator_1_eq));  // open: gt, lt
  Multiplexer #(.enable("false"), .select(2), .width(4)) multiplexer_2 (
    .in0(4'b0010), .in1(4'b0011), .in2(4'b0100), .in3(multiplexer_1_out), .out(ALU_Opcode),
    .sel(controlled_buffer_1_out));

  assign Imm5 = Instruction[10:6];
  assign Rd = Instruction[2:0];
  assign Rm = Instruction[5:3];

  // Other names for the same wires on the sheet: Instru[15:0] = Instruction; check5bit[4:0] = Instruction[15:11];
  //   part2[1:0] = Instruction[12:11]; part1[2:0] = Instruction[15:13]

  // Notes on the sheet:
  //   Note: ALU uses Rn register for shifts. Use Rn instead of Rm for shifts (immediate) here too
  //   Note 3: Imm32_Enable forces the use of the immediate for Rm register
  //   Note 2: MOV uses RSB ALU opcode with Imm8 reversed so that it is copied to output register
  //   Pull output low on Enable = 0
  //   only ADD and SUB use Rm
  //   Enable carry for SUB since it is reversed in ALU
  //   ALU will use Imm32 instead of Rm
endmodule
